# Fritzing sketch Robot_Evasor_Completo (saved by Fritzing 0.9.3b)
breadboards: 4
stripboards: 1

parts:
  Componente1 = Arduino Uno (Rev3)
  hc-sr1 = hc-sr04
  IC1 = L293D [package=THT]
  M1 = DC Motor
  M2 = DC Motor
  U1 = SWITCH_SPDT [package=kps-1290]
  hc-sr2 = hc-sr04
  hc-sr3 = hc-sr04

nets:
  N1: Componente1.D8, IC1.In_4
  N2: Componente1.D9_PWM, IC1.Enable_2
  N3: Componente1.D10_PWM/SS, IC1.In_3
  N4: Componente1.D11_PWM/MOSI, IC1.Enable_1
  N5: Componente1.D12/MISO, IC1.In_2
  N6: Componente1.D13/SCK, IC1.In_1
  N7: Componente1.D2, hc-sr3.Trig
  N8: Componente1.D3_PWM, hc-sr3.Echo
  N9: Componente1.D4, hc-sr1.Trig
  N10: Componente1.D5_PWM, hc-sr1.Echo
  N11: Componente1.D6_PWM, hc-sr2.Trig
  N12: Componente1.D7, hc-sr2.Echo
  VCC: Componente1.5V, hc-sr1.VCC, IC1.+V, hc-sr2.VCC, hc-sr3.VCC
  GND: Componente1.GND, hc-sr1.GND, IC1.0V, hc-sr2.GND, hc-sr3.GND
  N13: IC1.Out_1_(_Controlled_by_Enable_1_), M1.pin_1
  N14: IC1.Out_2_(_Controlled_by_Enable_1_), M1.pin_2
  N15: IC1.+Vmotor, U1.S
  N16: IC1.Out_3_(_Controlled_by_Enable_2_), M2.pin_2
  N17: IC1.Out_4_(_Controlled_by_Enable_2_), M2.pin_1

notes:
  Bateria Fuente Externa
