# Fritzing sketch Robot_Evasor_Ultrasonicos (saved by Fritzing 0.9.3b)
breadboards: 3

parts:
  Componente1 = Arduino Uno (Rev3)
  hc-sr1 = hc-sr04
  hc-sr2 = hc-sr04
  hc-sr3 = hc-sr04

nets:
  N1: Componente1.D2, hc-sr3.Trig
  N2: Componente1.D3_PWM, hc-sr3.Echo
  N3: Componente1.D4, hc-sr1.Trig
  N4: Componente1.D5_PWM, hc-sr1.Echo
  N5: Componente1.D6_PWM, hc-sr2.Trig
  N6: Componente1.D7, hc-sr2.Echo
  VCC: Componente1.5V, hc-sr1.VCC, hc-sr2.VCC, hc-sr3.VCC
  GND: Componente1.GND, hc-sr1.GND, hc-sr2.GND, hc-sr3.GND
