# Fritzing sketch Digrama L293D (saved by Fritzing 0.9.2b)
breadboards: 1

parts:
  Parte1 = Arduino Uno (Rev3) - ICSP
  IC1 = L293D [package=THT]
  M1 = DC Motor
  M2 = DC Motor
  VCC1 = 4 x AAA Battery Mount

nets:
  N1: Parte1.D2, IC1.In_2
  N2: Parte1.D3_PWM, IC1.In_1
  N3: Parte1.D4, IC1.In_3
  N4: Parte1.D5_PWM, IC1.In_4
  N5: Parte1.D6_PWM, IC1.Enable_1, IC1.Enable_2
  N6: Parte1.5V, IC1.+V
  N7: Parte1.GND, IC1.0V, VCC1.-
  N8: IC1.Out_1_(_Controlled_by_Enable_1_), M1.pin_1
  N9: IC1.Out_2_(_Controlled_by_Enable_1_), M1.pin_2
  N10: IC1.+Vmotor, VCC1.+
  N11: IC1.Out_3_(_Controlled_by_Enable_2_), M2.pin_2
  N12: IC1.Out_4_(_Controlled_by_Enable_2_), M2.pin_1
